# Fritzing sketch Colour Word Clock PCBV17 (saved by Fritzing 1.0.3b)
circuit board: 9.05553cm x 5.73728cm

parts:
  R5 = Resistor [tolerance=±5% resistance=470 power=0.25 package=THT]
  1000_uF = Electrolytic Capacitor [capacitance=1mF voltage=16V package="100 mil [THT, electrolytic]"]
  Part2 = Arduino Nano (Rev3.0) (ICSP)
  Bluetooth = male pin header, 6 pins [form="♂ (male)"]
  RTCclock2 = female pin header, 6 pins [form="♀ (female)"]
  LDR = male pin header, 2 pins [form="♂ (male)"]
  R13 = Resistor [tolerance=±5% resistance=22k power=0.25W package=THT]
  RTC-clock = female pin header, 6 pins [form="♀ (female)"]
  RTCclock5 = female pin header, 6 pins [form="♀ (female)"]
  RTCclock6 = female pin header, 3 pins [form="♀ (female)"]
  RTCclock4 = female pin header, 3 pins [form="♀ (female)"]
  RTCclock3 = female pin header, 3 pins [form="♀ (female)"]
  RTCclock7 = female pin header, 2 pins [form="♀ (female)"]
  RTCclock8 = female pin header, 6 pins [form="♀ (female)"]
  R16 = Resistor [tolerance=±5% resistance=1.1k power=0.25W package=THT]
  R17 = Resistor [tolerance=±5% resistance=2.2k power=0.25W package=THT]
  RTCclock9 = female pin header, 6 pins [form="♀ (female)"]
  RTCclock10 = female pin header, 6 pins [form="♀ (female)"]
  DCF = female pin header, 3 pins [form="♀ (female)"]
  R18 = Resistor [tolerance=±5% resistance=470 power=0.25W package=THT]
  RTCclock11 = female pin header, 4 pins [form="♀ (female)"]
  R19 = Resistor [tolerance=±5% resistance=470 power=0.25W package=THT]
  - = LED - 3mm [color="Red (633nm)" current=0.030A package="3 mm [THT]"]
  -_2 = LED - 3mm [color="Yellow (592nm)" current=0.030A package="3 mm [THT]"]
  Rotary = female pin header, 5 pins [form="♀ (female)"]
  J1 = screw terminal, 2 pins
  1N5817/4001 = Rectifier Diode [part_number=1N4001 package="300 mil [THT]"]
  5V_Out_GND = female pin header, 3 pins [form="♀ (female)"]
  AMS1117_3v3 = female pin header, 3 pins [form="♀ (female)"]
  JP1 = Jumper [package=sj_2s-no-ns]
  JP2 = Jumper [package=sj_2s-no-ns]
  JP4 = Jumper [package=sj_2s-no-ns]
  JP3 = Jumper [package=sj_2s-no-ns]

nets:
  N1: R5.Pin_0, RTCclock6.pin2
  N2: R5.Pin_1, Part2.D5
  N3: 1000_uF.-, Part2.GND, Bluetooth.pin4, R13.Pin_0, RTC-clock.pin1, RTCclock5.pin6, RTCclock6.pin1, RTCclock3.pin1, RTCclock3.pin2, RTCclock3.pin3, RTCclock7.pin2, R17.Pin_1, DCF.pin3, -.cathode, -_2.cathode, Rotary.pin5, J1.pin1, 5V_Out_GND.pin1, AMS1117_3v3.pin1
  N4: 1000_uF.+, RTCclock6.pin3, J1.pin2, 1N5817/4001.anode
  N5: Part2.D1/TX, JP1.2
  N6: Part2.D0/RX, JP2.2
  N7: Part2.D2, DCF.pin2
  N8: Part2.D3, Rotary.pin2
  N9: Part2.D4, Rotary.pin3
  N10: Part2.D6, JP3.2
  N11: Part2.D7, JP4.2
  N12: Part2.D8, Rotary.pin1
  N13: Part2.D9, R19.Pin_0
  N14: Part2.D10, R18.Pin_1, RTCclock11.pin2
  N15: Part2.D11/MOSI, RTCclock11.pin3
  N16: Part2.D12/MISO, RTCclock11.pin4
  N17: Part2.5V, Bluetooth.pin5, LDR.pin2, RTC-clock.pin2, RTCclock5.pin4, RTCclock4.pin1, RTCclock4.pin2, RTCclock4.pin3, RTCclock7.pin1, DCF.pin1, Rotary.pin4, 1N5817/4001.cathode, 5V_Out_GND.pin3, AMS1117_3v3.pin3
  N18: Part2.A5, RTC-clock.pin4
  N19: Part2.A4, RTC-clock.pin3
  N20: Part2.A2, LDR.pin1, R13.Pin_1
  N21: Bluetooth.pin2, RTCclock5.pin2, R16.Pin_1, R17.Pin_0
  N22: Bluetooth.pin3, RTCclock5.pin3, JP2.1, JP4.1
  N23: RTCclock2.pin1, RTCclock9.pin1
  N24: RTCclock2.pin2, RTCclock9.pin2
  N25: RTCclock2.pin3, RTCclock9.pin3
  N26: RTCclock2.pin4, RTCclock9.pin4
  N27: RTCclock2.pin5, RTCclock9.pin5
  N28: RTCclock2.pin6, RTCclock9.pin6
  N29: RTCclock8.pin1, RTCclock10.pin1
  N30: RTCclock8.pin2, RTCclock10.pin2
  N31: RTCclock8.pin3, RTCclock10.pin3
  N32: RTCclock8.pin4, RTCclock10.pin4
  N33: RTCclock8.pin5, RTCclock10.pin5
  N34: RTCclock8.pin6, RTCclock10.pin6
  N35: R16.Pin_0, JP1.1, JP3.1
  N36: R18.Pin_0, -.anode
  N37: RTCclock11.pin1, R19.Pin_1, -_2.anode
  N38: 5V_Out_GND.pin2, AMS1117_3v3.pin2

notes:
  +
  -
  Gnd
  5V
  32K
  SQW
  SCL
  SDA
  State
  <-RX
  TX->
  EN
  Power
  TX
  RX
  Key
  3V3
  A5
  A4
  D5
  DCF signal
  D8
  D3
  D4
  A3
  A2
  DT
  SW
  CLK
  D9
  D10
  D11
  D12
  >
  D6
  D7
  A1
  A6
  A7
  Vin
  Rst
  D2
  Solder D7 & D6 ------or------------ RX & TX
  A0
  Aref
  D13
  Signal to LED
  Signal
